# Fritzing sketch Sketch (saved by Fritzing 0.9.2b)
breadboards: 1

parts:
  Part2 = Arduino Uno (Rev3)
  S1 = Pushbutton [package="[THT]"]
  R3 = Resistor [tolerance=±5% resistance=220 package=THT]
  J1 = Basic Servo
  S2 = Pushbutton [package="[THT]"]
  R4 = Resistor [tolerance=±5% resistance=220 package=THT]
  S3 = Pushbutton [package="[THT]"]
  R5 = Resistor [tolerance=±5% resistance=220 package=THT]
  Part3 = SRF05 Ultrasonic Rangefinder
  LED1 = RGB LED (com. anode, rbg) [package="5 mm [THT]"]  # not connected

nets:
  N1: Part2.D9_PWM, J1.pulse
  N2: Part2.D12/MISO, Part3.Echo
  N3: Part2.D13/SCK, Part3.Trig
  GND: Part2.GND, R3.Pin_1, J1.gnd, R4.Pin_1, R5.Pin_1, Part3.GND
  N4: Part2.D2, S3.Pin_1, S3.Pin_2, R5.Pin_0
  N5: Part2.D4, S2.Pin_1, S2.Pin_2, R4.Pin_0
  N6: Part2.D7, S1.Pin_1, S1.Pin_2, R3.Pin_0
  VCC: Part2.5V, S1.Pin_3, S1.Pin_4, J1.vcc, S2.Pin_3, S2.Pin_4, S3.Pin_3, S3.Pin_4, Part3.VCC
